# Fritzing sketch breadboard (saved by Fritzing 0.9.3b)

parts:
  Raspberry_Pi_1 = Raspberry Pi 3 [part_number=RPI-3-V1.2]
  S4 = Flip Clock: Month [package=THT]
  S5 = Pushbutton [package=THT]
  S6 = Flip Clock: Days [package=THT]
  S7 = H-Bridge with L298N
  M1 = DC Motor
  VCC1 = 4 x AAA Battery Mount
  M2 = DC Motor

nets:
  N1: Raspberry_Pi_1.GIPO17, S7.IN4
  N2: Raspberry_Pi_1.GIPO27, S7.IN3
  N3: Raspberry_Pi_1.GIPO19, S7.IN2
  N4: Raspberry_Pi_1.GIPO26, S7.IN1
  GND: Raspberry_Pi_1.GND, S4.L1, S5.leg1, S6.L1, S7.GND, VCC1.-
  N5: Raspberry_Pi_1.GIPO12, S6.COM
  N6: Raspberry_Pi_1.GIPO7, S6.L2
  N7: Raspberry_Pi_1.GIPO8, S6.L3
  N8: Raspberry_Pi_1.GIPO25, S6.L4
  N9: Raspberry_Pi_1.GIPO24, S4.COM
  N10: Raspberry_Pi_1.GIPO23, S4.L2
  N11: Raspberry_Pi_1.GIPO18, S5.leg0
  N12: S7.12V, VCC1.+
  N13: S7.ENA, S7.ENA-5V
  N14: S7.M1-01, M1.pin_2
  N15: S7.M1-02, M1.pin_1
  N16: S7.M2-01, M2.pin_2
  N17: S7.M2-02, M2.pin_1

notes:
  AM/PM
  DAY

custom parts:
  H-Bridge with L298N: h-bridge
